# Fritzing sketch so_do_chan (saved by Fritzing 0.9.9b)

parts:
  Part1 = Arduino Uno (Rev3)
  Part2 = RFID-RC522-v2
  Part3 = LCD1602-I2C
  M2 = fc-51 [package=THT]
  M3 = fc-51 [package=THT]
  M4 = fc-51 [package=THT]
  M5 = fc-51 [package=THT]
  M6 = fc-51 [package=THT]
  M7 = fc-51 [package=THT]
  J1 = Basic Servo
  J2 = Basic Servo
  J3 = Piezo Speaker

nets:
  N1: Part1.A0, M7.pin1
  N2: Part1.A1, M2.pin1
  N3: Part1.A4/SDA, Part3.SDA
  N4: Part1.A5/SCL, Part3.SCL
  N5: Part1.D8, J3.pin2
  N6: Part1.D9_PWM, Part2.RST
  N7: Part1.D10_PWM/SS, Part2.SDA
  N8: Part1.D11_PWM/MOSI, Part2.MOSI
  N9: Part1.D12/MISO, Part2.MISO
  N10: Part1.D13/SCK, Part2.SCK
  GND: Part1.GND, Part2.GND, Part3.GND
  N11: Part1.D2, M3.pin1
  N12: Part1.D3_PWM, M4.pin1
  N13: Part1.D4, M5.pin1
  N14: Part1.D5_PWM, M6.pin1
  N15: Part1.D6_PWM, J1.pulse
  N16: Part1.D7, J2.pulse
  3V3: Part1.3V3, Part2.3.3V
  5V: Part1.5V, Part3.VCC

custom parts:
  RFID-RC522-v2: A simple China made RFID-RC522 Reader; do check the pin labels, as this is a MFRC522 based clone.
  LCD1602-I2C: A standard character display, usually with 2x16 characters. Comes in many colors with LCM1602 IIC attached.
